// Digital circuit matrix.dig as structural Verilog
module matrix (
  input  clk
);

  wire decoder_1_out_0, decoder_1_out_1, decoder_1_out_2, decoder_1_out_3, decoder_1_out_4, decoder_1_out_5,
       decoder_1_out_6, decoder_1_out_7, switch_1_b, switch_9_b, switch_17_b, switch_25_b, switch_33_b,
       switch_41_b, switch_49_b, switch_57_b, switchdt_1_p1, switchdt_1_p2;
  wire [2:0] counter_1_out;
  wire [7:0] switch_1_a;

  Switch switch_1 (.A(switch_1_a[0]), .B(switch_1_b));
  PullDown pulldown_1 (.out(switch_1_a[0]));
  Switch switch_2 (.A(switch_1_a[1]), .B(switch_1_b));
  PullDown pulldown_2 (.out(switch_1_a[1]));
  Switch switch_3 (.A(switch_1_a[2]), .B(switch_1_b));
  PullDown pulldown_3 (.out(switch_1_a[2]));
  Switch switch_4 (.A(switch_1_a[3]), .B(switch_1_b));
  PullDown pulldown_4 (.out(switch_1_a[3]));
  Switch switch_5 (.A(switch_1_a[4]), .B(switch_1_b));
  PullDown pulldown_5 (.out(switch_1_a[4]));
  Switch switch_6 (.A(switch_1_a[5]), .B(switch_1_b));
  PullDown pulldown_6 (.out(switch_1_a[5]));
  Switch switch_7 (.A(switch_1_a[6]), .B(switch_1_b));
  PullDown pulldown_7 (.out(switch_1_a[6]));
  Switch switch_8 (.A(switch_1_a[7]), .B(switch_1_b));
  PullDown pulldown_8 (.out(switch_1_a[7]));
  Switch switch_9 (.A(switch_1_a[0]), .B(switch_9_b));
  Switch switch_10 (.A(switch_1_a[1]), .B(switch_9_b));
  Switch switch_11 (.A(switch_1_a[2]), .B(switch_9_b));
  Switch switch_12 (.A(switch_1_a[3]), .B(switch_9_b));
  Switch switch_13 (.A(switch_1_a[4]), .B(switch_9_b));
  Switch switch_14 (.A(switch_1_a[5]), .B(switch_9_b));
  Switch switch_15 (.A(switch_1_a[6]), .B(switch_9_b));
  Switch switch_16 (.A(switch_1_a[7]), .B(switch_9_b));
  assign switch_1_b = decoder_1_out_0 ? decoder_1_out_0 : 1'bz;  // Driver driver_1
  Switch switch_17 (.A(switch_1_a[0]), .B(switch_17_b));
  Switch switch_18 (.A(switch_1_a[1]), .B(switch_17_b));
  Switch switch_19 (.A(switch_1_a[2]), .B(switch_17_b));
  Switch switch_20 (.A(switch_1_a[3]), .B(switch_17_b));
  Switch switch_21 (.A(switch_1_a[4]), .B(switch_17_b));
  Switch switch_22 (.A(switch_1_a[5]), .B(switch_17_b));
  Switch switch_23 (.A(switch_1_a[6]), .B(switch_17_b));
  Switch switch_24 (.A(switch_1_a[7]), .B(switch_17_b));
  assign switch_9_b = decoder_1_out_1 ? decoder_1_out_1 : 1'bz;  // Driver driver_2
  Switch switch_25 (.A(switch_1_a[0]), .B(switch_25_b));
  Switch switch_26 (.A(switch_1_a[1]), .B(switch_25_b));
  Switch switch_27 (.A(switch_1_a[2]), .B(switch_25_b));
  Switch switch_28 (.A(switch_1_a[3]), .B(switch_25_b));
  Switch switch_29 (.A(switch_1_a[4]), .B(switch_25_b));
  Switch switch_30 (.A(switch_1_a[5]), .B(switch_25_b));
  Switch switch_31 (.A(switch_1_a[6]), .B(switch_25_b));
  Switch switch_32 (.A(switch_1_a[7]), .B(switch_25_b));
  assign switch_17_b = decoder_1_out_2 ? decoder_1_out_2 : 1'bz;  // Driver driver_3
  Decoder #(.Selector_Bits(3)) decoder_1 (
    .sel(counter_1_out), .out_0(decoder_1_out_0), .out_1(decoder_1_out_1), .out_2(decoder_1_out_2),
    .out_3(decoder_1_out_3), .out_4(decoder_1_out_4), .out_5(decoder_1_out_5), .out_6(decoder_1_out_6),
    .out_7(decoder_1_out_7));
  Switch switch_33 (.A(switch_1_a[0]), .B(switch_33_b));
  Switch switch_34 (.A(switch_1_a[1]), .B(switch_33_b));
  Switch switch_35 (.A(switch_1_a[2]), .B(switch_33_b));
  Switch switch_36 (.A(switch_1_a[3]), .B(switch_33_b));
  Switch switch_37 (.A(switch_1_a[4]), .B(switch_33_b));
  Switch switch_38 (.A(switch_1_a[5]), .B(switch_33_b));
  Switch switch_39 (.A(switch_1_a[6]), .B(switch_33_b));
  Switch switch_40 (.A(switch_1_a[7]), .B(switch_33_b));
  assign switch_25_b = decoder_1_out_3 ? decoder_1_out_3 : 1'bz;  // Driver driver_4
  Switch switch_41 (.A(switch_1_a[0]), .B(switch_41_b));
  Switch switch_42 (.A(switch_1_a[1]), .B(switch_41_b));
  Switch switch_43 (.A(switch_1_a[2]), .B(switch_41_b));
  Switch switch_44 (.A(switch_1_a[3]), .B(switch_41_b));
  Switch switch_45 (.A(switch_1_a[4]), .B(switch_41_b));
  Switch switch_46 (.A(switch_1_a[5]), .B(switch_41_b));
  Switch switch_47 (.A(switch_1_a[6]), .B(switch_41_b));
  Switch switch_48 (.A(switch_1_a[7]), .B(switch_41_b));
  assign switch_33_b = decoder_1_out_4 ? decoder_1_out_4 : 1'bz;  // Driver driver_5
  Switch switch_49 (.A(switch_1_a[0]), .B(switch_49_b));
  Switch switch_50 (.A(switch_1_a[1]), .B(switch_49_b));
  Switch switch_51 (.A(switch_1_a[2]), .B(switch_49_b));
  Switch switch_52 (.A(switch_1_a[3]), .B(switch_49_b));
  Switch switch_53 (.A(switch_1_a[4]), .B(switch_49_b));
  Switch switch_54 (.A(switch_1_a[5]), .B(switch_49_b));
  Switch switch_55 (.A(switch_1_a[6]), .B(switch_49_b));
  Switch switch_56 (.A(switch_1_a[7]), .B(switch_49_b));
  assign switch_41_b = decoder_1_out_5 ? decoder_1_out_5 : 1'bz;  // Driver driver_6
  Switch switch_57 (.A(switch_1_a[0]), .B(switch_57_b));
  Switch switch_58 (.A(switch_1_a[1]), .B(switch_57_b));
  Switch switch_59 (.A(switch_1_a[2]), .B(switch_57_b));
  Switch switch_60 (.A(switch_1_a[3]), .B(switch_57_b));
  Switch switch_61 (.A(switch_1_a[4]), .B(switch_57_b));
  Switch switch_62 (.A(switch_1_a[5]), .B(switch_57_b));
  Switch switch_63 (.A(switch_1_a[6]), .B(switch_57_b));
  Switch switch_64 (.A(switch_1_a[7]), .B(switch_57_b));
  assign switch_49_b = decoder_1_out_6 ? decoder_1_out_6 : 1'bz;  // Driver driver_7
  assign switch_57_b = decoder_1_out_7 ? decoder_1_out_7 : 1'bz;  // Driver driver_8
  LedMatrix #(.ledPersistence("true")) ledmatrix_1 (.rows(switch_1_a), .column(counter_1_out));
  // SwitchDT switchdt_1: pin names not known; wires that end beside it: switchdt_1_p1, switchdt_1_p2, clk
  Counter #(.Bits(3)) counter_1 (.en(1'b1), .C(switchdt_1_p1), .clr(1'b0), .out(counter_1_out));  // open: ovf
  Button button_1 (.out(switchdt_1_p2));

  // Notes on the sheet:
  //   clk: Hz: 30
endmodule
